# Fritzing sketch Nixie IN12 PCB (saved by Fritzing 0.9.3b)
circuit board: 2.6cm x 3.7cm
breadboards: 1

parts:
  IN-12B = IN-12 Nixie tube [part_number=IN-12B]
  J5 = female pin header, 2 pins [form="♀ (female)"]
  J6 = female pin header, 2 pins [form="♀ (female)"]
  JP1 = Header 5x2 [package=avr_icsp]

nets:
  N1: IN-12B.Anode, J5.pin1, J5.pin2
  N2: IN-12B.Cathode_0, JP1.10
  N3: IN-12B.Cathode_1, JP1.1
  N4: IN-12B.Cathode_2, JP1.2
  N5: IN-12B.Cathode_3, JP1.3
  N6: IN-12B.Cathode_4, JP1.4
  N7: IN-12B.Cathode_5, JP1.5
  N8: IN-12B.Cathode_6, JP1.6
  N9: IN-12B.Cathode_7, JP1.7
  N10: IN-12B.Cathode_8, JP1.8
  N11: IN-12B.Cathode_9, JP1.9
  N12: IN-12B.Cathode_Comma, J6.pin1, J6.pin2

custom parts:
  IN-12 Nixie tube: Russian IN-12 Nixie neon indicator tube
