# Fritzing sketch Nixie_Main_PCB V131 (saved by Fritzing 0.9.3b)
circuit board: 11.5cm x 4.05cm

parts:
  IC2 = Voltage Regulator [package=to220-igo]
  JACK1 = 2.1mm DC Barrel Jack
  U2 = K155ID1 [package="DIP16 [THT]"]
  D1 = Rectifier Diode [part_number=1N4007 package="300 mil [THT]"]
  Q1 = MOSFET-NCHANNEL [part_number=IRF740 package=to220v]
  C2 = Ceramic Capacitor [capacitance=100nF package="100 mil [THT, multilayer]"]
  R1 = Resistor [tolerance=±5% resistance=1k package=THT]
  L1 = Inductor [inductance=330µH current=1A package="400 mil [THT]"]
  R2 = Resistor [tolerance=±5% resistance=2.2k package=THT]
  C3 = Ceramic Capacitor [capacitance=100nF package="100 mil [THT, multilayer]"]
  D2 = Rectifier Diode [part_number=FR104 package="300 mil [THT]"]
  L2 = Inductor [inductance=100µH package="400 mil [THT]"]
  C4 = Ceramic Capacitor [capacitance=100nF package="100 mil [THT, multilayer]"]
  C5 = Ceramic Capacitor [capacitance=100nF package="100 mil [THT, multilayer]"]
  R3 = Resistor [tolerance=±5% resistance=10k package=THT]
  R4 = Resistor [tolerance=±5% resistance=360k package=THT]
  R5 = Rotary Potentiometer (Small) [maximum_resistance=10kΩ package=THT]
  R6 = Resistor [tolerance=±5% resistance=1k package=THT]
  R7 = Resistor [tolerance=±5% resistance=1k package=THT]
  R8 = Resistor [tolerance=±5% resistance=1k package=THT]
  C7 = Ceramic Capacitor [capacitance=100nF package="100 mil [THT, multilayer]"]
  C8 = Ceramic Capacitor [capacitance=100nF package="100 mil [THT, multilayer]"]
  J1 = male pin header, 4 pins [form="♂ (male)" part_number="Nixies & Colon"]
  J2 = male pin header, 2 pins [form="♂ (male)" part_number=GND]
  J3 = male pin header, 3 pins [form="♂ (male)" part_number=Buttons]
  R9 = Resistor [tolerance=±5% resistance=10k package=THT]
  R10 = Resistor [tolerance=±5% resistance=10k package=THT]
  I2C = female pin header, 4 pins [form="♀ (female)" part_number=DS1307]
  R11 = Resistor [tolerance=±5% resistance=15k power=1W package=THT]
  R12 = Resistor [tolerance=±5% resistance=15k package=THT]
  R13 = Resistor [tolerance=±5% resistance=15k package=THT]
  R14 = Resistor [tolerance=±5% resistance=360k package=THT]
  C1 = Electrolytic Capacitor [capacitance=4.7µF voltage=20V package="100 mil [THT, electrolytic]"]
  C6 = Ceramic Capacitor [capacitance=100nF package="100 mil [THT, multilayer]"]
  U1 = TLP627-4 [package="DIP16 [THT]"]
  U3 = K155ID1 [package="DIP16 [THT]"]
  JP1 = Header 5x2 [part_number="Nixie 1-3-5" package=2x5-ra]
  JP2 = Header 5x2 [part_number="Nixie 2-4-6" package=2x5-ra]
  C9 = Electrolytic Capacitor [capacitance=47µF voltage=450V package="300 mil [THT, electrolytic]"]
  J6 = male pin header, 2 pins [form="♂ (male)" part_number=debugWire]
  IC1 = MICROCONTROLLER [package=dil28-3-simon-kit]
  XTAL1 = Crystal [frequency="8 MHz" package=THT]
  C10 = Ceramic Capacitor [capacitance=27pF package="100 mil [THT, multilayer]"]
  C11 = Ceramic Capacitor [capacitance=27pF package="100 mil [THT, multilayer]"]
  J5 = male pin header, 3 pins [form="♂ (male)" part_number=LDR]

nets:
  GND: IC2.GND, JACK1.switch, JACK1.sleeve, U2.GND, Q1.S, C2.0, C3.0, C4.0, C5.1, R5.leg1, R5.wiper, C7.1, C8.1, J2.pin1, J2.pin2, J3.pin3, I2C.pin1, C1.-, C6.0, U1.Cathode_1, U1.Cathode_2, U1.Cathode_3, U1.Cathode_4, U3.GND, C9.-, IC1.GND, IC1.PB6(XTAL1_TOSC1), IC1.AGND, XTAL1.pin_1, C10.0, C11.0, C11.1, J5.pin3
  12V: IC2.IN, D1.cathode, L1.pin_0, C1.+
  5V: IC2.OUT, U2.VCC, C2.1, L2.pin_0, L2.pin_1, C4.1, C5.0, R3.Pin_0, C7.0, C8.0, R9.Pin_0, R10.Pin_0, I2C.pin2, U3.VCC, IC1.VCC, IC1.AVCC, IC1.AREF, J5.pin2
  N1: JACK1.center, D1.anode
  N2: U2.Q8, JP1.8
  N3: U2.Q9, JP1.9
  N4: U2.IA, IC1.PD0(RXD)
  N5: U2.ID, IC1.PD3(INT1)
  N6: U2.IB, IC1.PD1(TXD)
  N7: U2.IC, IC1.PD2(INT0)
  N8: U2.Q2, JP1.2
  N9: U2.Q3, JP1.3
  N10: U2.Q7, JP1.7
  N11: U2.Q6, JP1.6
  N12: U2.Q4, JP1.4
  N13: U2.Q5, JP1.5
  N14: U2.Q1, JP1.1
  N15: U2.Q0, JP1.10
  N16: Q1.G, IC1.PB3(MOSI_OC2)
  N17: Q1.D, L1.pin_1, R2.Pin_0, D2.anode
  N18: R1.Pin_0, IC1.PB0(ICP)
  N19: R1.Pin_1, U1.Anode_1
  N20: R2.Pin_1, C3.1
  180V: D2.cathode, R4.Pin_0, U1.Collector_4, U1.Collector_3, U1.Collector_2, U1.Collector_1, C9.+
  N21: R3.Pin_1, C6.1, J6.pin2
  N22: R4.Pin_1, R5.leg2, IC1.PC0(ADC0)
  N23: R6.Pin_0, IC1.PB1(OC1A)
  N24: R6.Pin_1, U1.Anode_2
  N25: R7.Pin_0, IC1.PB2(SS_OC1B)
  N26: R7.Pin_1, U1.Anode_3
  N27: R8.Pin_0, IC1.PB4(MISO)
  N28: R8.Pin_1, U1.Anode_4
  N29: J1.pin1, R11.Pin_1
  N30: J1.pin2, R12.Pin_1
  N31: J1.pin3, R13.Pin_1
  N32: J1.pin4, R14.Pin_1
  N33: J3.pin1, R9.Pin_1, IC1.PC1(ADC1)
  N34: J3.pin2, R10.Pin_1, IC1.PC2(ADC2)
  N35: I2C.pin3, IC1.PC4(ADC4_SDA)
  N36: I2C.pin4, IC1.PC5(ADC5_SCL)
  N37: R11.Pin_0, U1.Emitter_1
  N38: R12.Pin_0, U1.Emitter_2
  N39: R13.Pin_0, U1.Emitter_3
  N40: R14.Pin_0, U1.Emitter_4
  N41: U3.Q8, JP2.8
  N42: U3.Q9, JP2.9
  N43: U3.IA, IC1.PD4(XCK_T0)
  N44: U3.ID, IC1.PD7(AIN1)
  N45: U3.IB, IC1.PD5(T1)
  N46: U3.IC, IC1.PD6(AIN0)
  N47: U3.Q2, JP2.2
  N48: U3.Q3, JP2.3
  N49: U3.Q7, JP2.7
  N50: U3.Q6, JP2.6
  N51: U3.Q4, JP2.4
  N52: U3.Q5, JP2.5
  N53: U3.Q1, JP2.1
  N54: U3.Q0, JP2.10
  N55: J6.pin1, IC1.PC6(_RESET)
  N56: IC1.PB7(XTAL2_TOSC2), XTAL1.pin_0, C10.1
  N57: IC1.PC3(ADC3), J5.pin1

notes:
  Nixie CLock V1.31
  Nixie 1-3-5
  Nixie 2-4-6
  WARNING HIGH VOLTAGE!
  Colon 56  34  12
  GND 5V  SDA  SCL
  LDR
  GND
  Buttons
  dW/reset
  GND 5V Sig

custom parts:
  2.1mm DC Barrel Jack: 2.1mm DC Barrel Jack with Thru-Hole Connectors (breadboardable)
  K155ID1: High voltage BCD decoder
  TLP627-4: 4way HV optocoupler
