# Fritzing sketch Nixie_Main_PCB V15 (saved by Fritzing 0.9.3b)
circuit board: 11.2cm x 4.05cm

parts:
  IC2 = Voltage Regulator [package=to220-igo]
  JACK1 = 2.1mm DC Barrel Jack
  U2 = K155ID1 [package="DIP16 [THT]"]
  D1 = Rectifier Diode [part_number=1N4007 package="300 mil [THT]"]
  Q1 = MOSFET-NCHANNEL [part_number=IRF740 package=to220v]
  C2 = Ceramic Capacitor [capacitance=100nF package="100 mil [THT, multilayer]"]
  R1 = Resistor [tolerance=±5% resistance=1k package=THT]
  L1 = Inductor [inductance=330µH current=1A package="400 mil [THT]"]
  R2 = Resistor [tolerance=±5% resistance=2.2k package=THT]
  C3 = Ceramic Capacitor [capacitance=100nF package="100 mil [THT, multilayer]"]
  D2 = Rectifier Diode [part_number=FR104 package="300 mil [THT]"]
  L2 = Inductor [inductance=100µH package="400 mil [THT]"]
  C4 = Ceramic Capacitor [capacitance=100nF package="100 mil [THT, multilayer]"]
  C5 = Ceramic Capacitor [capacitance=100nF package="100 mil [THT, multilayer]"]
  R3 = Resistor [tolerance=±5% resistance=10k package=THT]
  R4 = Resistor [tolerance=±5% resistance=360k package=THT]
  R6 = Resistor [tolerance=±5% resistance=1k package=THT]
  R7 = Resistor [tolerance=±5% resistance=1k package=THT]
  R8 = Resistor [tolerance=±5% resistance=1k package=THT]
  C7 = Ceramic Capacitor [capacitance=100nF package="100 mil [THT, multilayer]"]
  C8 = Ceramic Capacitor [capacitance=100nF package="100 mil [THT, multilayer]"]
  J1 = male pin header, 4 pins [form="♂ (male)" part_number="Nixies & Colon"]
  J2 = male pin header, 2 pins [form="♂ (male)" part_number=GND]
  R9 = Resistor [tolerance=±5% resistance=10k package=THT]
  R10 = Resistor [tolerance=±5% resistance=10k package=THT]
  J3 = female pin header, 4 pins [form="♀ (female)" part_number=I2C]
  R11 = Resistor [tolerance=±5% resistance=15k power=1W package=THT]
  R12 = Resistor [tolerance=±5% resistance=15k package=THT]
  R13 = Resistor [tolerance=±5% resistance=15k package=THT]
  R14 = Resistor [tolerance=±5% resistance=360k package=THT]
  C1 = Electrolytic Capacitor [capacitance=4.7µF voltage=20V package="100 mil [THT, electrolytic]"]
  C6 = Ceramic Capacitor [capacitance=100nF package="100 mil [THT, multilayer]"]
  U1 = TLP627-4 [part_number=TLP627-4 package="DIP16 [THT]"]
  U3 = K155ID1 [package="DIP16 [THT]"]
  JP1 = Header 5x2 [part_number="Nixie 1-3-5" package=2x5-ra]
  C9 = Electrolytic Capacitor [capacitance=47µF voltage=450V package="300 mil [THT, electrolytic]"]
  J6 = male pin header, 2 pins [form="♂ (male)" part_number=debugWire_Conn]
  IC1 = MICROCONTROLLER [part_number=ATmega328 package=dil28-3-simon-kit]
  XTAL1 = Crystal [frequency="8 MHz" package=THT]
  C10 = Ceramic Capacitor [capacitance=27pF package="100 mil [THT, multilayer]"]
  C11 = Ceramic Capacitor [capacitance=27pF package="100 mil [THT, multilayer]"]
  J5 = male pin header, 3 pins [form="♂ (male)" part_number=LDR_Conn]
  JP2 = Header 5x2 [part_number="Nixie 2-4-6" package=2x5-ra]
  J4 = male pin header, 3 pins [form="♂ (male)" part_number=Buttons]
  VR1 = TRIMPOT [part_number=10K package=3362u-2]
  U4 = DIODE-ZENER [part_number=5.1V package=diode-zener]
  J7 = male pin header, 3 pins [form="♂ (male)" part_number="HV out"]

nets:
  GND: IC2.GND, JACK1.switch, JACK1.sleeve, U2.GND, Q1.S, C2.0, C3.0, C4.0, C5.1, C7.1, C8.1, J2.pin1, J2.pin2, J3.pin1, C1.-, C6.0, U1.Cathode_1, U1.Cathode_2, U1.Cathode_3, U1.Cathode_4, U3.GND, C9.-, IC1.GND, IC1.AGND, C10.0, C11.0, J5.pin3, J4.pin3, VR1.WIPER, VR1.CW, U4.A, J7.pin3
  12V: IC2.IN, D1.cathode, L1.pin_0, C1.+
  5V: IC2.OUT, U2.VCC, C2.1, L2.pin_0, C5.0, R3.Pin_0, C7.0, C8.0, R9.Pin_0, R10.Pin_0, J3.pin2, U3.VCC, IC1.VCC
  N1: JACK1.center, D1.anode
  U2 Q8: U2.Q8, JP1.8
  U2 Q9: U2.Q9, JP1.9
  PD0 U2 IA: U2.IA, IC1.PD0(RXD)
  PD3 U2 ID: U2.ID, IC1.PD3(INT1)
  PD1 U2 IB: U2.IB, IC1.PD1(TXD)
  PD2 U2 IC: U2.IC, IC1.PD2(INT0)
  U2 Q2: U2.Q2, JP1.2
  U2 Q3: U2.Q3, JP1.3
  U2 Q7: U2.Q7, JP1.7
  U2 Q6: U2.Q6, JP1.6
  U2 Q4: U2.Q4, JP1.4
  U2 Q5: U2.Q5, JP1.5
  U2 Q1: U2.Q1, JP1.1
  U2 Q0: U2.Q0, JP1.10
  PB3 HV PWM: Q1.G, IC1.PB3(MOSI_OC2)
  HV Puls/PC1 Button 1: Q1.D, L1.pin_1, R2.Pin_0, D2.anode, R9.Pin_1, IC1.PC1(ADC1), J4.pin1, J7.pin2
  PB0 Nixie 12: R1.Pin_0, IC1.PB0(ICP)
  N2: R1.Pin_1, U1.Anode_1
  N3: R2.Pin_1, C3.1
  180V: D2.cathode, R4.Pin_0, U1.Collector_4, U1.Collector_3, U1.Collector_2, U1.Collector_1, C9.+, J7.pin1
  AVCC: L2.pin_1, C4.1, IC1.AVCC, IC1.AREF, J5.pin2
  Reset Circuit: R3.Pin_1, C6.1, J6.pin2
  PC0 HV Ref: R4.Pin_1, IC1.PC0(ADC0), VR1.CCW, U4.C
  PB1 Nixie 34: R6.Pin_0, IC1.PB1(OC1A)
  N4: R6.Pin_1, U1.Anode_2
  PB2 Nixie 56: R7.Pin_0, IC1.PB2(SS_OC1B)
  N5: R7.Pin_1, U1.Anode_3
  PB4 Colon: R8.Pin_0, IC1.PB4(MISO)
  N6: R8.Pin_1, U1.Anode_4
  Nixie 12: J1.pin1, R11.Pin_1
  Nixie 34: J1.pin2, R12.Pin_1
  Nixie 56: J1.pin3, R13.Pin_1
  Colon: J1.pin4, R14.Pin_1
  PC2 Button 2: R10.Pin_1, IC1.PC2(ADC2), J4.pin2
  PC4 SDA: J3.pin3, IC1.PC4(ADC4_SDA)
  PC5 SCL: J3.pin4, IC1.PC5(ADC5_SCL)
  N7: R11.Pin_0, U1.Emitter_1
  N8: R12.Pin_0, U1.Emitter_2
  N9: R13.Pin_0, U1.Emitter_3
  N10: R14.Pin_0, U1.Emitter_4
  U3 Q8: U3.Q8, JP2.8
  U3 Q9: U3.Q9, JP2.9
  PD4 U3 IA: U3.IA, IC1.PD4(XCK_T0)
  PD7 U3 ID: U3.ID, IC1.PD7(AIN1)
  PD5 U3 IB: U3.IB, IC1.PD5(T1)
  PD6 U3 IC: U3.IC, IC1.PD6(AIN0)
  U3 Q2: U3.Q2, JP2.2
  U3 Q3: U3.Q3, JP2.3
  U3 Q7: U3.Q7, JP2.7
  U3 Q6: U3.Q6, JP2.6
  U3 Q4: U3.Q4, JP2.4
  U3 Q5: U3.Q5, JP2.5
  U3 Q1: U3.Q1, JP2.1
  U3 Q0: U3.Q0, JP2.10
  Reset Pin: J6.pin1, IC1.PC6(_RESET)
  N11: IC1.PB6(XTAL1_TOSC1), XTAL1.pin_1, C11.1
  N12: IC1.PB7(XTAL2_TOSC2), XTAL1.pin_0, C10.1
  PC3 LDR: IC1.PC3(ADC3), J5.pin1

notes:
  Nixie CLock V1.5
  Nixie 1-3-5
  ! DANGER HIGH VOLTAGE!
  Colon 56  34  12
  GND 5V  SDA  SCL
  LDR
  GND
  Buttons
  dW/reset
  GND 5V Sig
  Nixie Clock, Nixie clock main PCB, 1.5
  Nixie 2-4-6

custom parts:
  2.1mm DC Barrel Jack: 2.1mm DC Barrel Jack with Thru-Hole Connectors (breadboardable)
  K155ID1: High voltage BCD decoder
  TLP627-4: 4way HV optocoupler
