# Fritzing sketch Nixie_Main_PCB_Old (saved by Fritzing 0.9.2b)
circuit board: 11.5cm x 4cm

parts:
  IC1 = MICROCONTROLLER [package=dil28-3-simon-kit]
  IC2 = Voltage Regulator [package=to220-igo]
  U1 = TLP627-4 [package="DIP16 [THT]"]
  JACK1 = 2.1mm DC Barrel Jack
  U2 = K155ID1 [package="DIP16 [THT]"]
  U3 = K155ID1 [package="DIP16 [THT]"]
  D1 = Rectifier Diode [part_number=1N4007 package="300 mil [THT]"]
  Q1 = MOSFET-NCHANNEL [package=to220v]
  C2 = Ceramic Capacitor [capacitance=100nF package="100 mil [THT, multilayer]"]
  R1 = Resistor [tolerance=±5% resistance=1k package=THT]
  L1 = Inductor [inductance=330µH current=1A package="400 mil [THT]"]
  R2 = Resistor [tolerance=±5% resistance=2.2k package=THT]
  C3 = Ceramic Capacitor [capacitance=100nF package="100 mil [THT, multilayer]"]
  D2 = Rectifier Diode [part_number=FR104 package="300 mil [THT]"]
  L2 = Inductor [inductance=100µH package="400 mil [THT]"]
  C4 = Ceramic Capacitor [capacitance=100nF package="100 mil [THT, multilayer]"]
  C5 = Ceramic Capacitor [capacitance=100nF package="100 mil [THT, multilayer]"]
  R3 = Resistor [tolerance=±5% resistance=10k package=THT]
  C6 = Ceramic Capacitor [capacitance=100nF package="100 mil [THT, multilayer]"]
  R4 = Resistor [tolerance=±5% resistance=330k package=THT]
  R5 = Rotary Potentiometer (Small) [maximum_resistance=100kΩ package=THT]
  R6 = Resistor [tolerance=±5% resistance=1k package=THT]
  R7 = Resistor [tolerance=±5% resistance=1k package=THT]
  R8 = Resistor [tolerance=±5% resistance=1k package=THT]
  C7 = Ceramic Capacitor [capacitance=100nF package="100 mil [THT, multilayer]"]
  C8 = Ceramic Capacitor [capacitance=100nF package="100 mil [THT, multilayer]"]
  C9 = Electrolytic Capacitor [capacitance=47µF voltage=500V package="200 mil [THT, electrolytic]"]
  J1 = male pin header, 4 pins [form="♂ (male)" part_number="Nixies & Colon"]
  J2 = male pin header, 2 pins [form="♂ (male)" part_number=GND]
  J3 = male pin header, 3 pins [form="♂ (male)" part_number=Buttons]
  R9 = Resistor [tolerance=±5% resistance=10k package=THT]
  R10 = Resistor [tolerance=±5% resistance=10k package=THT]
  JP1 = Header 5x2 [part_number="Nixie 1,3 en 5" package=2x5-ra]
  JP2 = Header 5x2 [part_number="Nixie 2,4 en 6" package=2x5-ra]
  J4 = female pin header, 4 pins [form="♀ (female)" part_number=DS1307]
  R11 = Resistor [tolerance=±5% resistance=33k package=THT]
  R12 = Resistor [tolerance=±5% resistance=33k package=THT]
  R13 = Resistor [tolerance=±5% resistance=33k package=THT]
  R14 = Resistor [tolerance=±5% resistance=360k package=THT]
  C1 = Electrolytic Capacitor [capacitance=4.7µF voltage=20V package="100 mil [THT, electrolytic]"]

nets:
  VCC: IC1.PC6(_RESET), U2.VCC, U3.VCC, R3.Pin_1, C6.1, C7.0, C8.0, J4.pin1
  N1: IC1.PD0(RXD), U2.IA
  N2: IC1.PD1(TXD), U2.IB
  N3: IC1.PD2(INT0), U2.IC
  N4: IC1.PD3(INT1), U2.ID
  N5: IC1.PD4(XCK_T0), U3.IA
  5V: IC1.VCC, IC2.OUT, C2.1, L2.pin_0, C5.0, R3.Pin_0, R9.Pin_0, R10.Pin_0, J4.pin2
  GND: IC1.GND, IC1.AGND, IC2.GND, U1.Cathode_1, U1.Cathode_2, U1.Cathode_3, U1.Cathode_4, JACK1.switch, JACK1.sleeve, U2.GND, U3.GND, Q1.S, C2.0, C3.0, C4.0, C5.1, C6.0, R5.leg1, R5.wiper, C7.1, C8.1, C9.-, J2.pin1, J2.pin2, J3.pin3, C1.-
  N6: IC1.PD5(T1), U3.IB
  N7: IC1.PD6(AIN0), U3.IC
  N8: IC1.PD7(AIN1), U3.ID
  N9: IC1.PB0(ICP), R1.Pin_0
  N10: IC1.PB1(OC1A), R6.Pin_0
  N11: IC1.PB2(SS_OC1B), R7.Pin_0
  N12: IC1.PB3(MOSI_OC2), Q1.G
  N13: IC1.PB4(MISO), R8.Pin_0
  N14: IC1.AVCC, IC1.AREF, L2.pin_1, C4.1
  N15: IC1.PC0(ADC0), R4.Pin_1, R5.leg2
  N16: IC1.PC1(ADC1), J3.pin1, R9.Pin_1
  N17: IC1.PC2(ADC2), J3.pin2, R10.Pin_1
  N18: IC1.PC4(ADC4_SDA), J4.pin3
  N19: IC1.PC5(ADC5_SCL), J4.pin4
  12V: IC2.IN, D1.cathode, L1.pin_0, C1.+
  N20: U1.Anode_1, R1.Pin_1
  N21: U1.Anode_2, R6.Pin_1
  N22: U1.Anode_3, R7.Pin_1
  N23: U1.Anode_4, R8.Pin_1
  N24: U1.Emitter_4, R14.Pin_0
  180V: U1.Collector_4, U1.Collector_3, U1.Collector_2, U1.Collector_1, D2.cathode, R4.Pin_0, C9.+
  N25: U1.Emitter_3, R13.Pin_0
  N26: U1.Emitter_2, R12.Pin_0
  N27: U1.Emitter_1, R11.Pin_0
  N28: JACK1.center, D1.anode
  N29: U2.Q8, JP1.8
  N30: U2.Q9, JP1.9
  N31: U2.Q2, JP1.2
  N32: U2.Q3, JP1.3
  N33: U2.Q7, JP1.7
  N34: U2.Q6, JP1.6
  N35: U2.Q4, JP1.4
  N36: U2.Q5, JP1.5
  N37: U2.Q1, JP1.1
  N38: U2.Q0, JP1.10
  N39: U3.Q8, JP2.8
  N40: U3.Q9, JP2.9
  N41: U3.Q2, JP2.2
  N42: U3.Q3, JP2.3
  N43: U3.Q7, JP2.7
  N44: U3.Q6, JP2.6
  N45: U3.Q4, JP2.4
  N46: U3.Q5, JP2.5
  N47: U3.Q1, JP2.1
  N48: U3.Q0, JP2.10
  N49: Q1.D, L1.pin_1, R2.Pin_0, D2.anode
  N50: R2.Pin_1, C3.1
  N51: J1.pin1, R11.Pin_1
  N52: J1.pin2, R12.Pin_1
  N53: J1.pin3, R13.Pin_1
  N54: J1.pin4, R14.Pin_1

custom parts:
  TLP627-4: 4way HV optocoupler
  2.1mm DC Barrel Jack: 2.1mm DC Barrel Jack with Thru-Hole Connectors (breadboardable)
  K155ID1: High voltage BCD decoder
